# Fritzing sketch Electronique (saved by Fritzing 0.9.2b)

parts:
  U6 = LM2596 voltage regulator [package=sot23-5]
  Battery_12V_12Ah = Battery 12V 12Ah
  Joystick_A = Thumb Joystick
  Joystick_B = Thumb Joystick
  Interrupteur = SWITCH_SPDT [package=kps-1290]
  Light_L = LEDs [package=led-0603]
  Light_R = LEDs [package=led-0603]
  Mega_2560_rev3 = Arduino Mega 2560 (Rev3)
  Motor_HR = DC Motor
  Motor_VR = DC Motor
  Motor_VL = DC Motor
  Motor_HL = DC Motor
  Dual_Bridge_Motors_H = L298 [package=multiwatt15]
  Dual_Bridge_Motors_V = L298 [package=multiwatt15]
  Dual_Bridge_Lights = L298 [package=multiwatt15]

nets:
  N1: U6.IN+, Battery_12V_12Ah.+, Dual_Bridge_Motors_V.CSA, Dual_Bridge_Lights.CSA
  N2: U6.IN-, Interrupteur.S
  N3: U6.OUT+, Mega_2560_rev3.VIN
  GND: U6.OUT-, Joystick_A.GND, Joystick_B.GND, Mega_2560_rev3.GND, Dual_Bridge_Motors_H.GND
  N4: Battery_12V_12Ah.-, Interrupteur.P
  N5: Joystick_A.SEL, Mega_2560_rev3.A15
  N6: Joystick_A.HORZ, Mega_2560_rev3.A14
  N7: Joystick_A.VERT, Mega_2560_rev3.A13
  VCC: Joystick_A.VCC, Joystick_B.VCC
  N8: Joystick_B.VERT, Mega_2560_rev3.A12
  N9: Light_L.A, Dual_Bridge_Lights.OUT2
  N10: Light_L.C, Dual_Bridge_Lights.OUT1
  N11: Light_R.A, Dual_Bridge_Lights.OUT4
  N12: Light_R.C, Dual_Bridge_Lights.OUT3
  N13: Mega_2560_rev3.D13_PWM, Dual_Bridge_Motors_V.ENB
  N14: Mega_2560_rev3.D12_PWM, Dual_Bridge_Motors_V.IN4
  N15: Mega_2560_rev3.D11_PWM, Dual_Bridge_Motors_V.IN3
  N16: Mega_2560_rev3.D10_PWM, Dual_Bridge_Motors_V.ENA
  N17: Mega_2560_rev3.D9_PWM, Dual_Bridge_Motors_V.IN2
  N18: Mega_2560_rev3.D8_PWM, Dual_Bridge_Motors_V.IN1
  N19: Mega_2560_rev3.D2_PWM, Dual_Bridge_Motors_H.IN4
  N20: Mega_2560_rev3.D3_PWM, Dual_Bridge_Motors_H.IN3
  N21: Mega_2560_rev3.D4_PWM, Dual_Bridge_Motors_H.ENA
  N22: Mega_2560_rev3.D5_PWM, Dual_Bridge_Motors_H.IN1
  N23: Mega_2560_rev3.D6_PWM, Dual_Bridge_Motors_H.IN2
  N24: Mega_2560_rev3.D7_PWM, Dual_Bridge_Motors_H.ENB
  N25: Mega_2560_rev3.D22, Dual_Bridge_Lights.IN3
  N26: Mega_2560_rev3.D23, Dual_Bridge_Lights.IN1
  N27: Mega_2560_rev3.D24, Dual_Bridge_Lights.IN4
  N28: Mega_2560_rev3.D25, Dual_Bridge_Lights.IN2
  N29: Mega_2560_rev3.D26, Dual_Bridge_Lights.ENB
  N30: Mega_2560_rev3.D27, Dual_Bridge_Lights.ENA
  N31: Motor_HR.pin_2, Dual_Bridge_Motors_H.OUT4
  N32: Motor_VR.pin_1, Dual_Bridge_Motors_H.OUT2
  N33: Motor_VR.pin_2, Dual_Bridge_Motors_H.OUT1
  N34: Motor_VL.pin_1, Dual_Bridge_Motors_V.OUT3
  N35: Motor_VL.pin_2, Dual_Bridge_Motors_V.OUT4
  N36: Motor_HL.pin_1, Dual_Bridge_Motors_V.OUT2
  N37: Motor_HL.pin_2, Dual_Bridge_Motors_V.OUT1

custom parts:
  LM2596 voltage regulator: V_REG MIC5219 Standard 500mA LDO voltage regulator in SOT-23 layout. Micrel part MIC5219. BP (by-pass) pin is used to lower output noise with 470pF cap, may be left open.
